# Fritzing sketch Rocket_STAB_1.1 (saved by Fritzing 0.9.3b)
circuit board: 15.689cm x 3.10791cm
breadboards: 1

parts:
  BMP180 = Adafruit BMP180
  MPU6050 = MPU-6050 Board GY-521 [form="♀ (female)" package=THT]
  ADXL377 = Adafruit ADXL377 [part_number="Adafruit #1413"]
  ADS1115 = ADS1115 16-bit ADC Breakout
  SERVO2 = male pin header, 3 pins [form="♂ (male)"]
  SERVO1 = male pin header, 3 pins [form="♂ (male)"]
  Raspberry_Pi_Zero1 = Raspberry Pi Zero

nets:
  3V3: BMP180.+5V, ADXL377.VIN, ADS1115.VDD, SERVO2.pin2, SERVO1.pin2, Raspberry_Pi_Zero1.3v3, Raspberry_Pi_Zero1.3V3
  GND: BMP180.GND, MPU6050.pin2, ADXL377.GND, ADS1115.GND, SERVO2.pin1, SERVO1.pin1, Raspberry_Pi_Zero1.GND
  N1: BMP180.SCL, MPU6050.pin3, ADS1115.SCL, Raspberry_Pi_Zero1.GPIO3
  N2: BMP180.SDA, MPU6050.pin4, ADS1115.SDA, Raspberry_Pi_Zero1.GPIO2
  N3: ADXL377.ZOUT, ADS1115.A2
  N4: ADXL377.YOUT, ADS1115.A1
  N5: ADXL377.XOUT, ADS1115.A0
  N6: ADS1115.A3, SERVO2.pin3, SERVO1.pin3

custom parts:
  Adafruit BMP180: This precision sensor from Bosch is the best low-cost sensing solution for measuring barometric pressure and temperature. Because pressure changes with altitude you can also use it as an altimeter! The sensor is soldered onto a PCB with a 3.3V regulator, I2C level shifter and pull-up resistors on the I2C pins. The BMP180 is the next-generation of sensors from Bosch, and replaces the BMP085.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
  MPU-6050 Board GY-521: Acelerometro y Giroscopio MPU-6050 Board GY-521
  Adafruit ADXL377: Hey rocket man (burnin' out your fuse out there alone) ever wonder how fast you're rocketing? The ADXL377 +-200g 3-axis accelerometer may be able to tell the answer. You read that right, this accelerometer can sense up to 200g's of force. Incredible! Not surprisingly, we couldn't say "no" to a breakout for this sensor. The sensor is soldered onto a PCB with four mounting holes (in case you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
  ADS1115 16-bit ADC Breakout: ADS1015 12-bit I2C ADC+PGA Breakout
