# Fritzing sketch Rocket_STAB_1_PWR_SUPPLY (saved by Fritzing 0.9.2b)
breadboards: 1

parts:
  U2 = LIPO-1000mAh [package=lipo-1000]
  Part4 = PowerBoost 500 Charger
  S2 = SWITCH-MOMENTARY-2 [package=tactile-switch-1101ne]
  Raspberry_Pi_Zero2 = Raspberry Pi Zero
  R2 = Resistor [tolerance=±5% resistance=10k package=THT]
  R3 = Resistor [tolerance=±5% resistance=100k package=THT]

nets:
  N1: U2.+, Part4.VBAT, S2.1
  GND: U2.-, Part4.GND, Raspberry_Pi_Zero2.GND, R3.Pin_1
  N2: Part4.ENABLE, S2.2, R2.Pin_1, R3.Pin_0
  N3: Part4.LBO, Raspberry_Pi_Zero2.GIPO15
  N4: Part4.5.0V, Raspberry_Pi_Zero2.5V
  N5: Raspberry_Pi_Zero2.GIPO14, R2.Pin_0

custom parts:
  PowerBoost 500 Charger: The PowerBoost 500C is a little DC/DC boost converter module that can be powered by any 3.7V LiIon/LiPoly battery, and convert the battery output to 5.2V DC for running your 5V projects. At its heart is a TPS61090 boost converter from TI. This boost converter chip has some really nice extras such as low battery detection, 2A internal switch, synchronous conversion, excellent efficiency, and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
